# Fritzing sketch Pressto_Fritzing (saved by Fritzing 0.9.2b)
breadboards: 1

parts:
  Arduino_Uno = Arduino Uno (Rev3)
  EasyDriver = EasyDriver_v44
  5v_Power = Power plug
  12v_Power = Power plug
  DOWN_BTN = Pushbutton [package="[THT]"]
  UP_BTN = Pushbutton [package="[THT]"]
  R1 = Resistor [tolerance=±5% resistance=100 package=THT]
  R2 = Resistor [tolerance=±5% resistance=100 package=THT]
  Nema_17_Stepper_Motor = Stepper Motor - Bipolar
  Temp_Sensor = LM35 Temperature Sensor [package="TO92 [THT]"]
  R3 = Resistor [tolerance=±5% resistance=4.7k package=THT]
  Hall_Sensor = mystery part, 3 pins [chip_label=A1394]
  C1 = Ceramic Capacitor [capacitance=100nF package="100 mil [THT, multilayer]"]
  PUMP = DC Motor
  AQA421VL = RELAY-SOLIDSTATE [package=relay-s108t02]
  120v_AC_Power = Power plug
  U2 = mystery part, 7 pins [chip_label=TA8428K part_number=TA8428K]

nets:
  N1: Arduino_Uno.D8, AQA421VL.+
  N2: Arduino_Uno.D12/MISO, DOWN_BTN.Pin_3, DOWN_BTN.Pin_4, R1.Pin_0
  N3: Arduino_Uno.D13/SCK, UP_BTN.Pin_3, UP_BTN.Pin_4, R2.Pin_0
  N4: Arduino_Uno.D0/RX, EasyDriver.MS1
  N5: Arduino_Uno.D1/TX, EasyDriver.MS2
  N6: Arduino_Uno.D2, EasyDriver.DIR
  N7: Arduino_Uno.D3_PWM, EasyDriver.STEP
  N8: Arduino_Uno.D4, Temp_Sensor.Vout, R3.Pin_0
  N9: Arduino_Uno.D5_PWM, Hall_Sensor.pin3
  N10: Arduino_Uno.D7, U2.pin2
  VIN: Arduino_Uno.VIN, 5v_Power.VCC, R1.Pin_1, R2.Pin_1, Temp_Sensor.+Vs, R3.Pin_1, Hall_Sensor.pin1, C1.1, U2.pin7
  GND: EasyDriver.GND, 12v_Power.GND
  N11: EasyDriver.V+, 12v_Power.VCC
  N12: EasyDriver.OUT2A, Nema_17_Stepper_Motor.D
  N13: EasyDriver.OUT2B, Nema_17_Stepper_Motor.B
  N14: EasyDriver.OUT1A, Nema_17_Stepper_Motor.A
  N15: EasyDriver.OUT1B, Nema_17_Stepper_Motor.C
  GND_2: EasyDriver.ENABLE, 5v_Power.GND, DOWN_BTN.Pin_1, DOWN_BTN.Pin_2, UP_BTN.Pin_1, UP_BTN.Pin_2, Temp_Sensor.GND, Hall_Sensor.pin2, C1.0, AQA421VL.-, U2.pin1, U2.pin4
  N16: PUMP.pin_1, U2.pin5
  N17: PUMP.pin_2, U2.pin3
  N18: AQA421VL.T1, 120v_AC_Power.VCC
  Heater 2: AQA421VL.T2
  Heater 1: 120v_AC_Power.GND

notes:
  Temperature Sensor
  Piston Stepper
  5v Power Source
  12v Power Source
  Hall Sensor
  Water Pump
  AC Source
  Relay
  Heater
